# Fritzing sketch crc (saved by Fritzing 0.9.6b)
breadboards: 2

parts:
  IC1 = DIP - 14 pins [chip_label=74LS86 package="DIP (Dual Inline) [THT]"]
  IC2 = DIP - 20 pins [chip_label=74LS273 package="DIP (Dual Inline) [THT]"]
  IC3 = DIP - 20 pins [chip_label=74LS273 package="DIP (Dual Inline) [THT]"]
  Part1 = Arduino Nano (Rev3.0)
  D2 = Rectifier Diode [part_number=1N4001 package="300 mil [THT]"]
  R1 = Resistor [tolerance=±5% power=0.25 resistance=100k package=THT]
  D1 = Rectifier Diode [part_number=1N4001 package="300 mil [THT]"]
  R2 = Rotary Potentiometer (Small) [maximum_resistance=100kΩ package=THT]
  LED1 = LED - 5mm [color="Red (633nm)" current=0.030 package="5 mm [THT]"]
  LED2 = LED - 5mm [color="Red (633nm)" current=0.030 package="5 mm [THT]"]
  LED3 = LED - 5mm [color="Red (633nm)" current=0.030 package="5 mm [THT]"]
  LED4 = LED - 5mm [color="Red (633nm)" current=0.030 package="5 mm [THT]"]
  R3 = Resistor [tolerance=±5% power=0.25 resistance=220 package=THT]
  R4 = Resistor [tolerance=±5% power=0.25 resistance=220 package=THT]
  R5 = Resistor [tolerance=±5% power=0.25 resistance=220 package=THT]
  R6 = Resistor [tolerance=±5% power=0.25 resistance=220 package=THT]
  LED5 = LED - 5mm [color="Red (633nm)" current=0.030 package="5 mm [THT]"]
  LED6 = LED - 5mm [color="Red (633nm)" current=0.030 package="5 mm [THT]"]
  LED7 = LED - 5mm [color="Red (633nm)" current=0.030 package="5 mm [THT]"]
  LED8 = LED - 5mm [color="Red (633nm)" current=0.030 package="5 mm [THT]"]
  R7 = Resistor [tolerance=±5% power=0.25 resistance=220 package=THT]
  R8 = Resistor [tolerance=±5% power=0.25 resistance=220 package=THT]
  R9 = Resistor [tolerance=±5% power=0.25 resistance=220 package=THT]
  R10 = Resistor [tolerance=±5% power=0.25 resistance=220 package=THT]
  LED9 = LED - 5mm [color="Red (633nm)" current=0.030 package="5 mm [THT]"]
  LED10 = LED - 5mm [color="Red (633nm)" current=0.030 package="5 mm [THT]"]
  LED11 = LED - 5mm [color="Red (633nm)" current=0.030 package="5 mm [THT]"]
  LED12 = LED - 5mm [color="Red (633nm)" current=0.030 package="5 mm [THT]"]
  LED13 = LED - 5mm [color="Red (633nm)" current=0.030 package="5 mm [THT]"]
  LED14 = LED - 5mm [color="Red (633nm)" current=0.030 package="5 mm [THT]"]
  LED15 = LED - 5mm [color="Red (633nm)" current=0.030 package="5 mm [THT]"]
  LED16 = LED - 5mm [color="Red (633nm)" current=0.030 package="5 mm [THT]"]
  R11 = Resistor [tolerance=±5% power=0.25 resistance=220 package=THT]
  R12 = Resistor [tolerance=±5% power=0.25 resistance=220 package=THT]
  R13 = Resistor [tolerance=±5% power=0.25 resistance=220 package=THT]
  R14 = Resistor [tolerance=±5% power=0.25 resistance=220 package=THT]
  R15 = Resistor [tolerance=±5% power=0.25 resistance=220 package=THT]
  R16 = Resistor [tolerance=±5% power=0.25 resistance=220 package=THT]
  R17 = Resistor [tolerance=±5% power=0.25 resistance=220 package=THT]
  R18 = Resistor [tolerance=±5% power=0.25 resistance=220 package=THT]
  LED17 = LED - 5mm [color="Red (633nm)" current=0.030 package="5 mm [THT]"]
  LED18 = LED - 5mm [color="Red (633nm)" current=0.030 package="5 mm [THT]"]
  R19 = Resistor [tolerance=±5% power=0.25 resistance=220 package=THT]
  R20 = Resistor [tolerance=±5% power=0.25 resistance=220 package=THT]
  LCD1 = LCD screen

nets (from the schematic view):
  N1: IC1.1A, IC1.2A, IC1.4A, D2.anode, R1.Pin_0, D1.anode
  N2: IC1.1B, IC2.5Q, LED10.anode
  N3: IC1.1Y, IC2.4D
  N4: IC1.2B, IC3.4Q, LED5.anode
  N5: IC1.2Y, IC3.3D
  GND: IC1.GND, IC2.GND, IC3.GND, Part1.GND, R2.leg2, R3.Pin_1, R4.Pin_1, R5.Pin_1, R6.Pin_1, R7.Pin_0, R8.Pin_0, R9.Pin_0, R10.Pin_0, R11.Pin_1, R12.Pin_0, R13.Pin_1, R14.Pin_1, R15.Pin_1, R16.Pin_0, R17.Pin_0, R18.Pin_0, R19.Pin_1, R20.Pin_1, LCD1.VSS, LCD1.R/W, LCD1.LED-
  N6: IC1.4Y, IC3.8D
  N7: IC1.4B, Part1.D3, LED18.anode
  VCC: IC1.VCC, IC2.VCC, IC3.VCC, Part1.5V, R1.Pin_1, LCD1.VDD, LCD1.LED+
  N8: IC2.CLR, IC3.CLR, Part1.D10
  N9: IC2.1Q, Part1.D12/MISO, D1.cathode, LED12.anode
  N10: IC2.1D, IC2.2Q, LED13.anode
  N11: IC2.2D, IC2.3Q, LED11.anode
  N12: IC2.3D, IC2.4Q, LED14.anode
  N13: IC2.CLK, IC3.CLK, Part1.D13/SCK
  N14: IC2.5D, IC2.6Q, LED15.anode
  N15: IC2.6D, IC2.7Q, LED16.anode
  N16: IC2.7D, IC2.8Q, LED9.anode
  N17: IC2.8D, IC3.1Q, LED8.anode
  N18: IC3.1D, IC3.2Q, LED7.anode
  N19: IC3.2D, IC3.3Q, LED6.anode
  N20: IC3.4D, IC3.5Q, LED4.anode
  N21: IC3.5D, IC3.6Q, LED3.anode
  N22: IC3.6D, IC3.7Q, LED2.anode
  N23: IC3.7D, IC3.8Q, LED1.anode
  N24: Part1.D2, LED17.anode
  N25: Part1.D4, LCD1.DB4
  N26: Part1.D5, LCD1.DB5
  N27: Part1.D6, LCD1.DB6
  N28: Part1.D7, LCD1.DB7
  N29: Part1.D8, LCD1.RS
  N30: Part1.D9, LCD1.E
  N31: Part1.D11/MOSI, D2.cathode
  N32: R2.wiper, LCD1.V0
  N33: LED1.cathode, R3.Pin_0
  N34: LED2.cathode, R4.Pin_0
  N35: LED3.cathode, R5.Pin_0
  N36: LED4.cathode, R6.Pin_0
  N37: LED5.cathode, R10.Pin_1
  N38: LED6.cathode, R9.Pin_1
  N39: LED7.cathode, R8.Pin_1
  N40: LED8.cathode, R7.Pin_1
  N41: LED9.cathode, R11.Pin_0
  N42: LED10.cathode, R14.Pin_0
  N43: LED11.cathode, R18.Pin_1
  N44: LED12.cathode, R16.Pin_1
  N45: LED13.cathode, R17.Pin_1
  N46: LED14.cathode, R12.Pin_1
  N47: LED15.cathode, R13.Pin_0
  N48: LED16.cathode, R15.Pin_0
  N49: LED17.cathode, R19.Pin_0
  N50: LED18.cathode, R20.Pin_0

custom parts:
  DIP - 14 pins: A DIP stand-in part for whatever IC you want. With 14 pins on a 300mil dual inline package (DIP) footprint.
  DIP - 20 pins: A DIP stand-in part for whatever IC you want. With 20 pins on a 300mil dual inline package (DIP) footprint.
